# Fritzing sketch Ex4_sketch (saved by Fritzing 0.9.10b)
breadboards: 1

parts:
  Part1 = Arduino Uno (Rev3) - ICSP
  S1 = Pushbutton [package="[THT]"]
  R1 = Resistor [tolerance=±5% power=0.25 resistance=220 package=THT]
  LED1 = LED - 5mm [color="Red (633nm)" current=0.030 package="5 mm [THT]"]
  R2 = Resistor [tolerance=±5% power=0.25 resistance=220 package=THT]

nets:
  N1: Part1.D8, S1.Pin_3, S1.Pin_4, R1.Pin_1
  N2: Part1.D9_PWM, LED1.cathode
  N3: Part1.GND, S1.Pin_1, S1.Pin_2, R2.Pin_1
  N4: Part1.3V3, R1.Pin_0
  N5: LED1.anode, R2.Pin_0
