# Fritzing sketch Ex13 (saved by Fritzing 0.9.10b)
breadboards: 1

parts:
  Part1 = Arduino Uno (Rev3)
  LED1 = LED - 5mm [color="Red (633nm)" current=0.030 package="5 mm [THT]"]
  LED2 = LED - 5mm [color="Red (633nm)" current=0.030 package="5 mm [THT]"]
  LED3 = LED - 5mm [color="Red (633nm)" current=0.030 package="5 mm [THT]"]
  LED4 = LED - 5mm [color="Red (633nm)" current=0.030 package="5 mm [THT]"]
  LED5 = LED - 5mm [color="Red (633nm)" current=0.030 package="5 mm [THT]"]
  R1 = Resistor [tolerance=±5% power=0.25 resistance=220 package=THT]
  R2 = Resistor [tolerance=±5% power=0.25 resistance=220 package=THT]
  R3 = Resistor [tolerance=±5% power=0.25 resistance=220 package=THT]
  R4 = Resistor [tolerance=±5% power=0.25 resistance=220 package=THT]
  R5 = Resistor [tolerance=±5% power=0.25 resistance=220 package=THT]
  S1 = Pushbutton [package="[THT]"]
  R6 = Resistor [tolerance=±5% power=0.25 resistance=220 package=THT]

nets:
  N1: Part1.D9_PWM, LED1.cathode
  N2: Part1.D10_PWM/SS, LED2.cathode
  N3: Part1.D11_PWM/MOSI, LED3.cathode
  N4: Part1.D12/MISO, LED4.cathode
  N5: Part1.D13/SCK, LED5.cathode
  N6: Part1.GND, R1.Pin_1, R2.Pin_1, R3.Pin_1, R4.Pin_1, R5.Pin_1, S1.Pin_1, S1.Pin_2
  N7: Part1.D2, S1.Pin_3, S1.Pin_4, R6.Pin_0
  N8: Part1.5V, R6.Pin_1
  N9: LED1.anode, R5.Pin_0
  N10: LED2.anode, R4.Pin_0
  N11: LED3.anode, R3.Pin_0
  N12: LED4.anode, R2.Pin_0
  N13: LED5.anode, R1.Pin_0
